// Logisim project mmu.circ as structural Verilog: 1 circuit, main circuit main
module main (
);

  wire and_1_out, EN_q, or_1_out, or_2_out, or_3_out, or_4_out, or_5_out, or_6_out, or_7_out, xor_1_out,
       xor_2_out, xor_3_out, xor_4_out, xor_5_out, xor_6_out, xor_7_out, xor_8_out;
  wire [2:0] BANK_q;
  wire [6:0] multiplexer_1_out, PAGE_q;
  wire [7:0] PAGE_TBL_data, PID_q;
  wire [15:0] IN_ADDR_q;
  wire [15:8] PAGE_TBL_data_2;

  Register #(.width(1)) EN (.Q(EN_q));  // open: D, en, clk, clr
  Register #(.width(16)) IN_ADDR (.Q(IN_ADDR_q));  // open: D, en, clk, clr
  Register #(.width(7)) PAGE (.D(IN_ADDR_q[15:9]), .Q(PAGE_q));  // open: en, clk, clr
  Register #(.width(3)) BANK (.Q(BANK_q));  // open: D, en, clk, clr
  Register PID (.Q(PID_q));  // open: D, en, clk, clr
  xor xor_1 (xor_1_out, PID_q[7], PAGE_TBL_data_2[15]);
  RAM #(.addrWidth(10), .dataWidth(16), .databus("bidir")) PAGE_TBL (
    .addr({BANK_q, PAGE_q}), .data({PAGE_TBL_data_2, PAGE_TBL_data}));  // open: we, oe, clk
  xor xor_2 (xor_2_out, PID_q[6], PAGE_TBL_data_2[14]);
  or or_1 (or_1_out, xor_1_out, xor_2_out);
  or or_2 (or_2_out, or_1_out, or_3_out);
  // NOT_Gate not_1 has open pins: in=and_1_out, out=open
  xor xor_3 (xor_3_out, PID_q[5], PAGE_TBL_data_2[13]);
  xor xor_4 (xor_4_out, PID_q[4], PAGE_TBL_data_2[12]);
  or or_3 (or_3_out, xor_3_out, xor_4_out);
  and and_1 (and_1_out, or_4_out, EN_q);
  xor xor_5 (xor_5_out, PID_q[3], PAGE_TBL_data_2[11]);
  or or_4 (or_4_out, or_2_out, or_6_out);
  xor xor_6 (xor_6_out, PID_q[2], PAGE_TBL_data_2[10]);
  or or_5 (or_5_out, xor_5_out, xor_6_out);
  or or_6 (or_6_out, or_5_out, or_7_out);
  Multiplexer #(.width(7)) multiplexer_1 (
    .in0(IN_ADDR_q[15:9]), .in1(PAGE_TBL_data[6:0]), .out(multiplexer_1_out), .sel(EN_q));
  xor xor_7 (xor_7_out, PID_q[1], PAGE_TBL_data_2[9]);
  xor xor_8 (xor_8_out, PID_q[0], PAGE_TBL_data_2[8]);
  or or_7 (or_7_out, xor_7_out, xor_8_out);
  RAM #(.addrWidth(19)) MAIN_RAM (.addr({BANK_q, multiplexer_1_out, IN_ADDR_q[8:0]}));  // open: we, oe, clk, din, dout
endmodule
